# Fritzing sketch Arduino-Weighto (saved by Fritzing 0.9.9b)
breadboards: 1

parts:
  Part1 = Arduino Uno (Rev3) - ICSP
  Part2 = HX711 Weighing Sensor Module
  Part3 = HX711 Weighing Sensor Module
  Part4 = HX711 Weighing Sensor Module
  Part5 = HX711 Weighing Sensor Module

nets:
  N1: Part1.D2, Part2.CK/TX, Part3.CK/TX, Part4.CK/TX, Part5.CK/TX
  N2: Part1.D3_PWM, Part3.DO/RX
  N3: Part1.D4, Part2.DO/RX
  N4: Part1.D5_PWM, Part4.DO/RX
  N5: Part1.D6_PWM, Part5.DO/RX
  5V: Part1.5V, Part5.VCC
  GND: Part1.GND, Part3.GND
  VCC: Part2.VCC, Part3.VCC, Part4.VCC
  GND_2: Part2.GND, Part4.GND, Part5.GND
