# Fritzing sketch RPi-LED (saved by Fritzing 0.9.9b)
breadboards: 1

parts:
  U1 = WS2812 RGB LED strip
  Raspberry_Pi_1 = Raspberry Pi 3 [part_number=RPI-3-V1.2]
  Power_plug1 = Power plug

nets:
  GND: U1.GND, Raspberry_Pi_1.GND, Power_plug1.GND
  VCC: U1.VCC, Power_plug1.VCC
  N1: U1.DIN, Raspberry_Pi_1.GPIO18

custom parts:
  WS2812 RGB LED strip: WS2812 strip
